# Fritzing sketch CircuitDiagram (saved by Fritzing 0.9.2b)
breadboards: 1

parts:
  Part1 = Arduino Uno (Rev3)
  Q2 = PHOTOTRANSISTOR REFLECTIVE OBJECT SENSOR [package=qrb1114-side]
  R1 = Resistor [tolerance=±5% resistance=200 package=THT]
  R2 = Resistor [tolerance=±5% resistance=20k package=THT]
  R3 = Resistor [tolerance=±5% resistance=200 package=THT]
  R5 = Resistor [tolerance=±5% resistance=20k package=THT]
  Part3 = Rotoshield - Motor driver shield for Arduino
  Q1 = PHOTOTRANSISTOR REFLECTIVE OBJECT SENSOR [package=qrb1114-side]
  M1 = DC Motor
  M2 = DC Motor
  J1 = Power Jack [package=power_jack_combo]

nets:
  N1: Part1.A0, R5.Pin_1, Q1.A
  N2: Part1.A1, Q2.A, R2.Pin_1
  N3: Part1.5V, R1.Pin_0, R2.Pin_0, R3.Pin_0, R5.Pin_0
  N4: Part1.GND, Q2.C, Q2.K, Q1.C, Q1.K
  N5: Q2.E, R1.Pin_1
  N6: R3.Pin_1, Q1.E
  N7: Part3.M1-2, M2.pin_2
  N8: Part3.M1-1, M2.pin_1
  N9: Part3.M2-2, M1.pin_2
  N10: Part3.M2-1, M1.pin_1
  N11: Part3.VCC, J1.GNDBREAK
  GND: Part3.GND, J1.GND

notes:
  20KΩ
  200Ω
